# Fritzing sketch DO_NHIET_DO (saved by Fritzing 0.9.2b)
circuit board: 7.62104cm x 5.58569cm
breadboards: 1

parts:
  NGUON = Power plug
  7805 = Voltage Regulator - 5V [package="TO220 [THT]"]
  U2 = atmega168 [package=dip]
  XTAL1 = Crystal [frequency="16 Mhz" package=THT]
  C2 = Ceramic Capacitor [capacitance=100nF package="100 mil [THT, multilayer]"]
  C3 = Ceramic Capacitor [capacitance=100nF package="100 mil [THT, multilayer]"]
  LED1 = LED - 5mm [color="Red (633nm)" package="5 mm [THT]"]
  R1 = Resistor [tolerance=±5% resistance=220 package=THT]
  C1 = Electrolytic Capacitor [capacitance=1µF package="100 mil [THT, electrolytic]"]
  DS18B20 = female pin header, 3 pins [form="♀ (female)"]
  R2 = Resistor [tolerance=±5% resistance=4.7k package=THT]
  S2 = Momentary Switch [package=tactile-pth]
  S5 = Momentary Switch [package=tactile-pth]
  S4 = Momentary Switch [package=tactile-pth]
  S3 = Momentary Switch [package=tactile-pth]
  R5 = Resistor [tolerance=±5% resistance=10k package=THT]
  R6 = Resistor [tolerance=±5% resistance=10k package=THT]
  R7 = Resistor [tolerance=±5% resistance=10k package=THT]
  R3 = Resistor [tolerance=±5% resistance=100 package=THT]
  BUZER = Buzzer 12mm [package=buzzer-12mm]
  OLED096 = female pin header, 4 pins [form="♀ (female)"]
  R4 = Resistor [tolerance=±5% resistance=10k package=THT]

nets:
  N1: NGUON.VCC, 7805.input_voltage
  GND: NGUON.GND, 7805.GND, U2.GND, C2.0, C3.0, LED1.cathode, C1.-, DS18B20.pin3, S2.1, S5.1, S4.1, S3.2, BUZER.2, OLED096.pin1
  5V: 7805.output_voltage, U2.VCC, R1.Pin_0, C1.+, DS18B20.pin1, OLED096.pin2
  D2: U2.D2, R2.Pin_1
  D3: U2.D3_(PWM), R3.Pin_1
  XLAT1: U2.XLAT1, XTAL1.pin_0, C3.1
  XLAT2: U2.XLAT2, XTAL1.pin_1, C2.1
  D5: U2.D5_(PWM), R4.Pin_1
  D6: U2.D6_(PWM), R5.Pin_1
  D7: U2.D7, R6.Pin_1
  D8: U2.D8, R7.Pin_1
  A4: U2.A4
  A5: U2.A5, OLED096.pin3
  N2: LED1.anode, R1.Pin_1
  N3: DS18B20.pin2, R2.Pin_0
  N4: S2.3, R5.Pin_0
  N5: S5.3, R4.Pin_0
  N6: S4.3, R6.Pin_0
  N7: S3.3, R7.Pin_0
  N8: R3.Pin_0, BUZER.1
